# Fritzing sketch Generic WiFi (saved by Fritzing 0.9.4)
breadboards: 1

parts:
  U1 = ESP8266 WiFi Module [part_number=ESP8266]
  R3 = Resistor [tolerance=±5% resistance=120 package=THT]
  R4 = Resistor [tolerance=±5% resistance=220 package=THT]
  LED1 = LED - 3mm [color="Yellow (592nm)" package="3 mm [THT]"]
  R5 = Resistor [tolerance=±5% resistance=330 package=THT]
  S1 = Pushbutton [package="[THT]"]
  R6 = Resistor [tolerance=±5% resistance=10k package=THT]

nets:
  N1: U1.RXD, R3.Pin_1, R4.Pin_0
  N2: U1.VCC, U1.CH_PD, R6.Pin_1
  N3: U1.RST, S1.Pin_1, S1.Pin_2, R6.Pin_0
  N4: U1.GPIO_2, LED1.anode
  N5: U1.GND, R4.Pin_1, R5.Pin_0, S1.Pin_3, S1.Pin_4
  N6: LED1.cathode, R5.Pin_1

notes:
  From 3.3v Supply
  From Arduino Serial Tx
  To Arduino Serial Rx

custom parts:
  ESP8266 WiFi Module: Generic WiFi Module based on the ESP8266 with onboard PCB antenna and UART communications
